// Logisim project 1.FULL_ADDER.circ as structural Verilog: 5 circuits, main circuit main
module main (
  input  X,
  input  Y,
  input  Z,
  output Sum,
  output Carry
);

  wire X_Y_out, X_Z_out, XOR_out, Y_Z_out;

  xor XOR (XOR_out, Y, Z);
  and X_Z (X_Z_out, X, Z);
  and X_Y (X_Y_out, X, Y);
  and Y_Z (Y_Z_out, Y, Z);
  xor XOR_2 (Sum, X, XOR_out);
  or OR (Carry, X_Z_out, X_Y_out, Y_Z_out);

  // Notes on the sheet:
  //   FULL ADDER
endmodule

module testing (
  input  X,
  input  Y,
  input  Z,
  output SUM,
  output CARRY
);

  wire not_1_out, not_2_out, not_3_out, not_4_out, not_5_out, not_6_out, X_prime_Y_out,
       X_prime_Y_prime_Z_out, X_prime_Y_Y_nX__Z_out, X_prime_Y_Y_prime_X_out, X_prime_Y_Z_prime_out, X_Y_out,
       X_Y_prime_Z_prime_out, X_Y_Z_out, Y_prime_X_out;

  not not_1 (not_1_out, X);
  not not_2 (not_2_out, X);
  not not_3 (not_3_out, X);
  not not_4 (not_4_out, X);
  not not_5 (not_5_out, X);
  not not_6 (not_6_out, X);
  and X_prime_Y_prime_Z (X_prime_Y_prime_Z_out, not_1_out, not_2_out, X);
  and X_prime_Y_Z_prime (X_prime_Y_Z_prime_out, not_3_out, X, not_4_out);
  and X_Y_prime_Z_prime (X_Y_prime_Z_prime_out, X, not_5_out, not_6_out);
  and X_Y_Z (X_Y_Z_out, X, X, X);
  and X_Y (X_Y_out, X, X);
  and X_prime_Y (X_prime_Y_out, not_1_out, X);
  and Y_prime_X (Y_prime_X_out, not_2_out, X);
  or X_prime_Y_Y_prime_X (X_prime_Y_Y_prime_X_out, X_prime_Y_out, Y_prime_X_out);
  or X_prime_Y_prime_Z_X_prime_Y_Z_prime_X_Y_prime_Z_prime_X_Y_Z (SUM, X_prime_Y_prime_Z_out, X_prime_Y_Z_prime_out, X_Y_prime_Z_prime_out, X_Y_Z_out);
  and X_prime_Y_Y_nX__Z (X_prime_Y_Y_nX__Z_out, X_prime_Y_Y_prime_X_out, X);
  or XY__X_prime_Y_Y_prime_X_Z (CARRY, X_Y_out, X_prime_Y_Y_nX__Z_out);

  assign Y = X;
  assign Z = X;
endmodule

module simulator (
  input  A,
  input  B,
  input  C,
  output Sum,
  output Diffrence
);

  main main_1 (.X(A), .Y(B), .Z(C), .Sum(Sum), .Carry(Diffrence));
endmodule

module half_adder (
  input  X,
  input  Y,
  output Sum,
  output Carry
);

  xor xor_1 (Sum, X, Y);
  and and_1 (Carry, X, Y);
endmodule

module Full_Adder_Using_Half_Adder (
  input  A,
  input  B,
  input  Cin,
  output Sum,
  output Cout
);

  wire half_adder_1_carry, half_adder_1_sum, half_adder_2_carry;

  half_adder half_adder_1 (.X(A), .Y(B), .Sum(half_adder_1_sum), .Carry(half_adder_1_carry));
  half_adder half_adder_2 (.X(half_adder_1_sum), .Y(Cin), .Sum(Sum), .Carry(half_adder_2_carry));
  or or_1 (Cout, half_adder_2_carry, half_adder_1_carry);
endmodule
