// Logisim project BCDTOEXCESS3.circ as structural Verilog: 1 circuit, main circuit main
module main (
  input  D,
  input  C,
  input  B,
  input  A,
  output W,
  output X,
  output Y,
  output Z
);

  wire and_1_out, and_2_out, and_3_out, and_4_out, and_5_out, not_2_out, not_3_out, not_4_out;

  not not_1 (Z, D);
  not not_2 (not_2_out, C);
  not not_3 (not_3_out, A);
  not not_4 (not_4_out, B);
  and and_1 (and_1_out, B, C);
  and and_2 (and_2_out, B, D);
  and and_3 (and_3_out, not_4_out, C);
  and and_4 (and_4_out, not_4_out, D);
  and and_5 (and_5_out, B, not_2_out, Z);
  xnor xnor_1 (Y, C, D);
  or or_1 (W, A, and_1_out, and_2_out);
  or or_2 (X, and_3_out, and_4_out, and_5_out);
endmodule
