// Logisim project EXCESS3TOBCD.circ as structural Verilog: 1 circuit, main circuit main
module main (
  input  W,
  input  X,
  input  Y,
  input  Z,
  output A,
  output B,
  output C,
  output D
);

  wire and_1_out, and_2_out, and_3_out, and_4_out, and_5_out, not_1_out, not_2_out, not_3_out;

  not not_1 (not_1_out, W);
  not not_2 (not_2_out, X);
  not not_3 (not_3_out, Y);
  not not_4 (D, Z);
  and and_1 (and_1_out, W, X);
  and and_2 (and_2_out, W, Y, Z);
  and and_3 (and_3_out, not_2_out, not_3_out);
  and and_4 (and_4_out, not_2_out, D);
  and and_5 (and_5_out, X, Y, Z);
  xor xor_1 (C, Y, Z);
  or or_1 (A, and_1_out, and_2_out);
  or or_2 (B, and_3_out, and_4_out, and_5_out);
endmodule
