// Logisim project GRAYTOBCD.circ as structural Verilog: 1 circuit, main circuit main
module main (
  input  G3,
  input  G2,
  input  G1,
  input  G0,
  output B3,
  output B2,
  output B1,
  output B0
);

  wire and_2_out, and_3_out, and_4_out, and_5_out, and_6_out, and_7_out, and_8_out, not_1_out, not_2_out,
       not_3_out, not_4_out;

  not not_1 (not_1_out, G3);
  not not_2 (not_2_out, G2);
  not not_3 (not_3_out, G0);
  not not_4 (not_4_out, G1);
  and and_1 (B2, not_1_out, G2);
  and and_2 (and_2_out, not_2_out, G1);
  and and_3 (and_3_out, not_1_out, G2, not_4_out);
  and and_4 (and_4_out, not_2_out, G1, not_3_out);
  and and_5 (and_5_out, G2, G1, G0);
  and and_6 (and_6_out, G3, G0);
  and and_7 (and_7_out, not_2_out, not_4_out, G0);
  and and_8 (and_8_out, not_1_out, G2, not_4_out, not_3_out);
  or or_1 (B1, and_2_out, and_3_out);
  or or_2 (B0, and_4_out, and_5_out, and_6_out, and_7_out, and_8_out);

  assign B3 = G3;
endmodule
